// Logisim project main.circ as structural Verilog: 5 circuits, main circuit main
module main (
  input  in_1,
  input  [15:0] in_2,
  input  in_3,
  input  in_4,
  output [15:0] out_5
);

  wire clock_1_out;

  Clock clock_1 (.out(clock_1_out));
  counter counter_1 (.in_1(clock_1_out), .in_2(in_1), .in_3(in_2), .out_6(out_5), .in_4(in_3), .in_5(in_4));
endmodule

module high_register (
  input  in_1,
  input  [7:0] in_2,
  input  in_3,
  output [7:0] out_4
);

  wire [7:0] d_ff_1_q;

  D_Flip_Flop #(.trigger("high")) d_ff_1 (.clk(in_1), .D(in_2[0]), .Q(d_ff_1_q[0]));  // open: Qn, preset, en, reset
  D_Flip_Flop #(.trigger("high")) d_ff_2 (.clk(in_1), .D(in_2[1]), .Q(d_ff_1_q[1]));  // open: Qn, preset, en, reset
  D_Flip_Flop #(.trigger("high")) d_ff_3 (.clk(in_1), .D(in_2[2]), .Q(d_ff_1_q[2]));  // open: Qn, preset, en, reset
  D_Flip_Flop #(.trigger("high")) d_ff_4 (.clk(in_1), .D(in_2[3]), .Q(d_ff_1_q[3]));  // open: Qn, preset, en, reset
  D_Flip_Flop #(.trigger("high")) d_ff_5 (.clk(in_1), .D(in_2[4]), .Q(d_ff_1_q[4]));  // open: Qn, preset, en, reset
  D_Flip_Flop #(.trigger("high")) d_ff_6 (.clk(in_1), .D(in_2[5]), .Q(d_ff_1_q[5]));  // open: Qn, preset, en, reset
  D_Flip_Flop #(.trigger("high")) d_ff_7 (.clk(in_1), .D(in_2[6]), .Q(d_ff_1_q[6]));  // open: Qn, preset, en, reset
  D_Flip_Flop #(.trigger("high")) d_ff_8 (.clk(in_1), .D(in_2[7]), .Q(d_ff_1_q[7]));  // open: Qn, preset, en, reset
  assign out_4 = in_3 ? d_ff_1_q : 8'bz;  // Controlled_Buffer controlled_buffer_1
endmodule

module low_register (
  input  in_1,
  input  [7:0] in_2,
  input  in_3,
  output [7:0] out_4
);

  wire [7:0] d_ff_1_q;

  D_Flip_Flop #(.trigger("low")) d_ff_1 (.clk(in_1), .D(in_2[0]), .Q(d_ff_1_q[0]));  // open: Qn, preset, en, reset
  D_Flip_Flop #(.trigger("low")) d_ff_2 (.clk(in_1), .D(in_2[1]), .Q(d_ff_1_q[1]));  // open: Qn, preset, en, reset
  D_Flip_Flop #(.trigger("low")) d_ff_3 (.clk(in_1), .D(in_2[2]), .Q(d_ff_1_q[2]));  // open: Qn, preset, en, reset
  D_Flip_Flop #(.trigger("low")) d_ff_4 (.clk(in_1), .D(in_2[3]), .Q(d_ff_1_q[3]));  // open: Qn, preset, en, reset
  D_Flip_Flop #(.trigger("low")) d_ff_5 (.clk(in_1), .D(in_2[4]), .Q(d_ff_1_q[4]));  // open: Qn, preset, en, reset
  D_Flip_Flop #(.trigger("low")) d_ff_6 (.clk(in_1), .D(in_2[5]), .Q(d_ff_1_q[5]));  // open: Qn, preset, en, reset
  D_Flip_Flop #(.trigger("low")) d_ff_7 (.clk(in_1), .D(in_2[6]), .Q(d_ff_1_q[6]));  // open: Qn, preset, en, reset
  D_Flip_Flop #(.trigger("low")) d_ff_8 (.clk(in_1), .D(in_2[7]), .Q(d_ff_1_q[7]));  // open: Qn, preset, en, reset
  assign out_4 = in_3 ? d_ff_1_q : 8'bz;  // Controlled_Buffer controlled_buffer_1
endmodule

module counter (
  input  in_1,
  input  in_2,
  input  [15:0] in_3,
  input  in_4,
  input  in_5,
  output [15:0] out_6
);

  wire n2_bit_counter_1_out_9, n2_bit_counter_2_out_9, n2_bit_counter_3_out_9, n2_bit_counter_4_out_9,
       n2_bit_counter_5_out_9, n2_bit_counter_6_out_9, n2_bit_counter_7_out_9;

  _2_bit_counter u_2_bit_counter_1 (
    .clk(in_1), .enable(in_2), .d1(in_3[0]), .d2(in_3[1]), .inp_count(in_4), .reset(in_5), .out_7(out_6[0]),
    .out_8(out_6[1]), .out_9(n2_bit_counter_1_out_9));
  _2_bit_counter u_2_bit_counter_2 (
    .clk(in_1), .enable(n2_bit_counter_1_out_9), .d1(in_3[2]), .d2(in_3[3]), .inp_count(in_4), .reset(in_5),
    .out_7(out_6[2]), .out_8(out_6[3]), .out_9(n2_bit_counter_2_out_9));
  _2_bit_counter u_2_bit_counter_3 (
    .clk(in_1), .enable(n2_bit_counter_2_out_9), .d1(in_3[4]), .d2(in_3[5]), .inp_count(in_4), .reset(in_5),
    .out_7(out_6[4]), .out_8(out_6[5]), .out_9(n2_bit_counter_3_out_9));
  _2_bit_counter u_2_bit_counter_4 (
    .clk(in_1), .enable(n2_bit_counter_3_out_9), .d1(in_3[6]), .d2(in_3[7]), .inp_count(in_4), .reset(in_5),
    .out_7(out_6[6]), .out_8(out_6[7]), .out_9(n2_bit_counter_4_out_9));
  _2_bit_counter u_2_bit_counter_5 (
    .clk(in_1), .enable(n2_bit_counter_4_out_9), .d1(in_3[8]), .d2(in_3[9]), .inp_count(in_4), .reset(in_5),
    .out_7(out_6[8]), .out_8(out_6[9]), .out_9(n2_bit_counter_5_out_9));
  _2_bit_counter u_2_bit_counter_6 (
    .clk(in_1), .enable(n2_bit_counter_5_out_9), .d1(in_3[10]), .d2(in_3[11]), .inp_count(in_4),
    .reset(in_5), .out_7(out_6[10]), .out_8(out_6[11]), .out_9(n2_bit_counter_6_out_9));
  _2_bit_counter u_2_bit_counter_7 (
    .clk(in_1), .enable(n2_bit_counter_6_out_9), .d1(in_3[12]), .d2(in_3[13]), .inp_count(in_4),
    .reset(in_5), .out_7(out_6[12]), .out_8(out_6[13]), .out_9(n2_bit_counter_7_out_9));
  _2_bit_counter u_2_bit_counter_8 (
    .clk(in_1), .enable(n2_bit_counter_7_out_9), .d1(in_3[14]), .d2(in_3[15]), .inp_count(in_4),
    .reset(in_5), .out_7(out_6[14]), .out_8(out_6[15]));  // open: out_9
endmodule

module _2_bit_counter (
  input  clk,
  input  enable,
  input  d1,
  input  d2,
  input  inp_count,
  input  reset,
  output out_7,
  output out_8,
  output out_9
);

  wire and_1_out, and_2_out, d_ff_1_qn, multiplexer_1_out, multiplexer_2_out, or_1_out, xor_1_out;

  and and_1 (and_1_out, inp_count, clk);
  or or_1 (or_1_out, and_1_out, and_2_out);
  and and_2 (and_2_out, clk, enable);
  Multiplexer #(.enable("false")) multiplexer_1 (.in0(d_ff_1_qn), .in1(d1), .out(multiplexer_1_out), .sel(inp_count));
  D_Flip_Flop #(.trigger("falling")) d_ff_1 (
    .clk(or_1_out), .D(multiplexer_1_out), .Q(out_7), .Qn(d_ff_1_qn), .reset(reset));  // open: preset, en
  xor xor_1 (xor_1_out, out_7, out_8);
  Multiplexer #(.enable("false")) multiplexer_2 (.in0(xor_1_out), .in1(d2), .out(multiplexer_2_out), .sel(inp_count));
  D_Flip_Flop #(.trigger("falling")) d_ff_2 (
    .clk(or_1_out), .D(multiplexer_2_out), .Q(out_8), .reset(reset));  // open: Qn, preset, en
  and and_3 (out_9, out_7, enable, out_8);
endmodule
